// Logisim project DemoProj.circ as structural Verilog
module main (
);

  rom rom_1 ();  // open: addr, data
  alu alu_1 ();  // open: a, b, alu_op, result, flag_eq, flag_lt
  ee8_cpu ee8_cpu_1 ();  // open: clk, rst, rom_data, rom_addr, seven_seg
  instruction_decoder instruction_decoder_1 ();  // open: instruction, opcode, rs1, rs2, rd, immediate
endmodule

// VHDL entity ee8_cpu, as the project stores it:
-- EE8 CPU Top Level
-- Integrates all components for Logisim Evolution

library IEEE;
use IEEE.STD_LOGIC_1164.ALL;

entity ee8_cpu is
    Port (
        clk       : in  STD_LOGIC;                      -- System clock
        rst       : in  STD_LOGIC;                      -- Reset
        rom_data  : in  STD_LOGIC_VECTOR(15 downto 0);  -- Instruction from ROM
        rom_addr  : out STD_LOGIC_VECTOR(7 downto 0);   -- Address to ROM (PC)
        seven_seg : out STD_LOGIC_VECTOR(7 downto 0)    -- 7-segment output (RO)
    );
end ee8_cpu;

architecture Structural of ee8_cpu is

    -- Component declarations
    component alu is
        Port (
            a       : in  STD_LOGIC_VECTOR(7 downto 0);
            b       : in  STD_LOGIC_VECTOR(7 downto 0);
            alu_op  : in  STD_LOGIC_VECTOR(3 downto 0);
            result  : out STD_LOGIC_VECTOR(7 downto 0);
            flag_eq : out STD_LOGIC;
            flag_lt : out STD_LOGIC
        );
    end component;

    component register_file is
        Port (
            clk     : in  STD_LOGIC;
            rst     : in  STD_LOGIC;
            we      : in  STD_LOGIC;
            sel_rs1 : in  STD_LOGIC_VECTOR(1 downto 0);
            sel_rs2 : in  STD_LOGIC_VECTOR(1 downto 0);
            sel_rd  : in  STD_LOGIC_VECTOR(1 downto 0);
            data_in : in  STD_LOGIC_VECTOR(7 downto 0);
            rs1_out : out STD_LOGIC_VECTOR(7 downto 0);
            rs2_out : out STD_LOGIC_VECTOR(7 downto 0);
            ro_out  : out STD_LOGIC_VECTOR(7 downto 0);
            rf_out  : out STD_LOGIC_VECTOR(7 downto 0)
        );
    end component;

    component instruction_decoder is
        Port (
            instruction : in  STD_LOGIC_VECTOR(15 downto 0);
            opcode      : out STD_LOGIC_VECTOR(3 downto 0);
            rs1         : out STD_LOGIC_VECTOR(1 downto 0);
            rs2         : out STD_LOGIC_VECTOR(1 downto 0);
            rd          : out STD_LOGIC_VECTOR(1 downto 0);
            immediate   : out STD_LOGIC_VECTOR(7 downto 0)
        );
    end component;

    component program_counter is
        Port (
            clk         : in  STD_LOGIC;
            rst         : in  STD_LOGIC;
            halt        : in  STD_LOGIC;
            jump        : in  STD_LOGIC;
            branch      : in  STD_LOGIC;
            branch_cond : in  STD_LOGIC;
            flag_rf     : in  STD_LOGIC_VECTOR(7 downto 0);
            jump_addr   : in  STD_LOGIC_VECTOR(7 downto 0);
            pc_out      : out STD_LOGIC_VECTOR(7 downto 0)
        );
    end component;

    component control_unit is
        Port (
            opcode      : in  STD_LOGIC_VECTOR(3 downto 0);
            reg_write   : out STD_LOGIC;
            alu_op      : out STD_LOGIC_VECTOR(3 downto 0);
            imm_sel     : out STD_LOGIC;
            jump        : out STD_LOGIC;
            branch      : out STD_LOGIC;
            branch_cond : out STD_LOGIC;
            halt        : out STD_LOGIC;
            flag_write  : out STD_LOGIC
        );
    end component;

    -- Internal signals: Instruction decoder outputs
    signal opcode    : STD_LOGIC_VECTOR(3 downto 0);
    signal rs1_sel   : STD_LOGIC_VECTOR(1 downto 0);
    signal rs2_sel   : STD_LOGIC_VECTOR(1 downto 0);
    signal rd_sel    : STD_LOGIC_VECTOR(1 downto 0);
    signal immediate : STD_LOGIC_VECTOR(7 downto 0);

    -- Internal signals: Control unit outputs
    signal reg_write   : STD_LOGIC;
    signal alu_op      : STD_LOGIC_VECTOR(3 downto 0);
    signal imm_sel     : STD_LOGIC;
    signal jump        : STD_LOGIC;
    signal branch      : STD_LOGIC;
    signal branch_cond : STD_LOGIC;
    signal halt        : STD_LOGIC;
    signal flag_write  : STD_LOGIC;

    -- Internal signals: Register file outputs
    signal rs1_data : STD_LOGIC_VECTOR(7 downto 0);
    signal rs2_data : STD_LOGIC_VECTOR(7 downto 0);
    signal rf_data  : STD_LOGIC_VECTOR(7 downto 0);  -- RF register for branch conditions

    -- Internal signals: ALU
    signal alu_a      : STD_LOGIC_VECTOR(7 downto 0);
    signal alu_result : STD_LOGIC_VECTOR(7 downto 0);
    signal flag_eq    : STD_LOGIC;
    signal flag_lt    : STD_LOGIC;

    -- Internal signals: Register write data and destination
    signal reg_data_in : STD_LOGIC_VECTOR(7 downto 0);
    signal reg_rd_sel  : STD_LOGIC_VECTOR(1 downto 0);

    -- Internal signals: Program counter
    signal pc_value : STD_LOGIC_VECTOR(7 downto 0);

begin

    -- Instruction Decoder
    inst_decoder: instruction_decoder
        port map (
            instruction => rom_data,
            opcode      => opcode,
            rs1         => rs1_sel,
            rs2         => rs2_sel,
            rd          => rd_sel,
            immediate   => immediate
        );

    -- Control Unit
    ctrl_unit: control_unit
        port map (
            opcode      => opcode,
            reg_write   => reg_write,
            alu_op      => alu_op,
            imm_sel     => imm_sel,
            jump        => jump,
            branch      => branch,
            branch_cond => branch_cond,
            halt        => halt,
            flag_write  => flag_write
        );

    -- ALU input selection
    -- For LDI: pass immediate through ALU (via MOV operation)
    alu_a <= immediate when imm_sel = '1' else rs1_data;

    -- ALU
    alu_inst: alu
        port map (
            a       => alu_a,
            b       => rs2_data,
            alu_op  => alu_op,
            result  => alu_result,
            flag_eq => flag_eq,
            flag_lt => flag_lt
        );

    -- Register destination selection
    -- For LDI: destination comes from rs1 field (instruction[11:10])
    -- For flag ops (LT/EQ): destination is RF (11)
    -- Otherwise: destination is rd field
    reg_rd_sel <= "11" when flag_write = '1' else
                  rs1_sel when imm_sel = '1' else
                  rd_sel;

    -- Register write data is always ALU result
    reg_data_in <= alu_result;

    -- Register File
    reg_file: register_file
        port map (
            clk     => clk,
            rst     => rst,
            we      => reg_write,
            sel_rs1 => rs1_sel,
            sel_rs2 => rs2_sel,
            sel_rd  => reg_rd_sel,
            data_in => reg_data_in,
            rs1_out => rs1_data,
            rs2_out => rs2_data,
            ro_out  => seven_seg,
            rf_out  => rf_data
        );

    -- Program Counter
    pc_inst: program_counter
        port map (
            clk         => clk,
            rst         => rst,
            halt        => halt,
            jump        => jump,
            branch      => branch,
            branch_cond => branch_cond,
            flag_rf     => rf_data,
            jump_addr   => immediate,
            pc_out      => pc_value
        );

    -- ROM address is PC
    rom_addr <= pc_value;

end Structural;

// VHDL entity alu, as the project stores it:
-- EE8 CPU Arithmetic Logic Unit
-- Performs all arithmetic and logical operations

library IEEE;
use IEEE.STD_LOGIC_1164.ALL;
use IEEE.NUMERIC_STD.ALL;

entity alu is
    Port (
        a       : in  STD_LOGIC_VECTOR(7 downto 0);  -- Operand A (Rs1)
        b       : in  STD_LOGIC_VECTOR(7 downto 0);  -- Operand B (Rs2)
        alu_op  : in  STD_LOGIC_VECTOR(3 downto 0);  -- Operation select
        result  : out STD_LOGIC_VECTOR(7 downto 0);  -- ALU result
        flag_eq : out STD_LOGIC;                      -- Equality flag
        flag_lt : out STD_LOGIC                       -- Less-than flag
    );
end alu;

architecture Behavioral of alu is
    signal shift_amount : integer range 0 to 7;
begin
    -- Extract shift amount from lower 3 bits of b
    shift_amount <= to_integer(unsigned(b(2 downto 0)));

    process(a, b, alu_op, shift_amount)
        variable a_unsigned : unsigned(7 downto 0);
        variable b_unsigned : unsigned(7 downto 0);
    begin
        a_unsigned := unsigned(a);
        b_unsigned := unsigned(b);

        -- Default outputs
        result <= (others => '0');
        flag_eq <= '0';
        flag_lt <= '0';

        case alu_op is
            when "0000" =>  -- ADD
                result <= std_logic_vector(a_unsigned + b_unsigned);

            when "0001" =>  -- SUB
                result <= std_logic_vector(a_unsigned - b_unsigned);

            when "0010" =>  -- AND
                result <= a and b;

            when "0011" =>  -- OR
                result <= a or b;

            when "0100" =>  -- XOR
                result <= a xor b;

            when "0101" =>  -- SHL (shift left)
                result <= std_logic_vector(shift_left(a_unsigned, shift_amount));

            when "0110" =>  -- SHR (shift right)
                result <= std_logic_vector(shift_right(a_unsigned, shift_amount));

            when "0111" =>  -- MOV (passthrough A)
                result <= a;

            when "1000" =>  -- LT (less than comparison)
                if a_unsigned < b_unsigned then
                    flag_lt <= '1';
                    result <= x"01";
                else
                    flag_lt <= '0';
                    result <= x"00";
                end if;

            when "1001" =>  -- EQ (equality comparison)
                if a_unsigned = b_unsigned then
                    flag_eq <= '1';
                    result <= x"01";
                else
                    flag_eq <= '0';
                    result <= x"00";
                end if;

            when others =>
                result <= (others => '0');
        end case;
    end process;

end Behavioral;

// VHDL entity instruction_decoder, as the project stores it:
-- EE8 CPU Instruction Decoder
-- Extracts fields from 16-bit instruction word

library IEEE;
use IEEE.STD_LOGIC_1164.ALL;

entity instruction_decoder is
    Port (
        instruction : in  STD_LOGIC_VECTOR(15 downto 0);  -- Full instruction word
        opcode      : out STD_LOGIC_VECTOR(3 downto 0);   -- Bits [15:12]
        rs1         : out STD_LOGIC_VECTOR(1 downto 0);   -- Bits [11:10]
        rs2         : out STD_LOGIC_VECTOR(1 downto 0);   -- Bits [9:8]
        rd          : out STD_LOGIC_VECTOR(1 downto 0);   -- Bits [7:6]
        immediate   : out STD_LOGIC_VECTOR(7 downto 0)    -- Bits [7:0]
    );
end instruction_decoder;

architecture Behavioral of instruction_decoder is
begin
    -- Pure combinational field extraction
    opcode    <= instruction(15 downto 12);
    rs1       <= instruction(11 downto 10);
    rs2       <= instruction(9 downto 8);
    rd        <= instruction(7 downto 6);
    immediate <= instruction(7 downto 0);
end Behavioral;

// VHDL entity rom, as the project stores it:
-- EE8 CPU Program ROM
-- 256 x 16-bit ROM with preloaded test program
-- Students can modify the rom_data array with their own programs

library IEEE;
use IEEE.STD_LOGIC_1164.ALL;
use IEEE.NUMERIC_STD.ALL;

entity rom is
    Port (
        addr : in  STD_LOGIC_VECTOR(7 downto 0);   -- 8-bit address from PC
        data : out STD_LOGIC_VECTOR(15 downto 0)   -- 16-bit instruction output
    );
end rom;

architecture Behavioral of rom is
    -- ROM type: 256 entries of 16-bit instructions
    type rom_array_t is array (0 to 255) of STD_LOGIC_VECTOR(15 downto 0);

    -- =========================================================================
    -- INSTRUCTION ENCODING REFERENCE:
    -- =========================================================================
    -- Format: [15:12]=opcode [11:10]=rs1 [9:8]=rs2 [7:6]=rd [5:0]=unused
    --         [7:0]=immediate (for LDI, JMP, JZ, JNZ)
    --
    -- REGISTERS: R0=00, R1=01, RO=10, RF=11
    --
    -- OPCODES:
    --   0x0=ADD  rs1+rs2->rd     0x8=LT   (rs1<rs2)->RF
    --   0x1=SUB  rs1-rs2->rd     0x9=EQ   (rs1=rs2)->RF
    --   0x2=AND  rs1&rs2->rd     0xA=LDI  imm->rs1
    --   0x3=OR   rs1|rs2->rd     0xB=JMP  PC=imm
    --   0x4=XOR  rs1^rs2->rd     0xC=JZ   if RF=0: PC=imm
    --   0x5=SHL  rs1<<rs2->rd    0xD=JNZ  if RF!=0: PC=imm
    --   0x6=SHR  rs1>>rs2->rd    0xE=NOP
    --   0x7=MOV  rs1->rd         0xF=HALT
    --
    -- ENCODING EXAMPLES:
    --   LDI R0, 10:     1010_00_xx_0000_1010 = 0xA00A
    --   LDI R1, 5:      1010_01_xx_0000_0101 = 0xA405
    --   ADD R0, R1, RO: 0000_00_01_10_000000 = 0x0180
    --   MOV R0, x, RO:  0111_00_xx_10_000000 = 0x7080
    --   LT R0, R1:      1000_00_01_xx_xxxxxx = 0x8100
    --   JNZ 2:          1101_xx_xx_0000_0010 = 0xD002
    --   HALT:           1111_xx_xx_xxxx_xxxx = 0xF000
    -- =========================================================================

    -- =========================================================================
    -- TEST PROGRAM: Basic arithmetic
    -- Expected result: RO = 15 (0x0F)
    -- =========================================================================
    constant rom_data : rom_array_t := (
        0  => x"A00A",  -- LDI R0, 10      ; R0 = 10
        1  => x"A405",  -- LDI R1, 5       ; R1 = 5
        2  => x"0180",  -- ADD R0, R1, RO  ; RO = R0 + R1 = 15
        3  => x"F000",  -- HALT            ; Stop execution

        -- Remaining addresses filled with NOP
        others => x"E000"
    );

begin
    -- Combinational read (active on address change)
    data <= rom_data(to_integer(unsigned(addr)));
end Behavioral;

// VHDL entity register_file, as the project stores it:
-- EE8 CPU Register File
-- 4 x 8-bit registers: R0, R1, RO, RF

library IEEE;
use IEEE.STD_LOGIC_1164.ALL;
use IEEE.NUMERIC_STD.ALL;

entity register_file is
    Port (
        clk     : in  STD_LOGIC;                      -- Clock
        rst     : in  STD_LOGIC;                      -- Async reset
        we      : in  STD_LOGIC;                      -- Write enable
        sel_rs1 : in  STD_LOGIC_VECTOR(1 downto 0);   -- Source register 1 select
        sel_rs2 : in  STD_LOGIC_VECTOR(1 downto 0);   -- Source register 2 select
        sel_rd  : in  STD_LOGIC_VECTOR(1 downto 0);   -- Destination register select
        data_in : in  STD_LOGIC_VECTOR(7 downto 0);   -- Write data
        rs1_out : out STD_LOGIC_VECTOR(7 downto 0);   -- Source 1 data
        rs2_out : out STD_LOGIC_VECTOR(7 downto 0);   -- Source 2 data
        ro_out  : out STD_LOGIC_VECTOR(7 downto 0);   -- RO register (for 7-seg)
        rf_out  : out STD_LOGIC_VECTOR(7 downto 0)    -- RF register (for branch cond)
    );
end register_file;

architecture Behavioral of register_file is
    -- Register array: R0(00), R1(01), RO(10), RF(11)
    type reg_array_t is array (0 to 3) of STD_LOGIC_VECTOR(7 downto 0);
    signal registers : reg_array_t;
begin

    -- Synchronous write with async reset
    process(clk, rst)
    begin
        if rst = '1' then
            registers(0) <= (others => '0');  -- R0
            registers(1) <= (others => '0');  -- R1
            registers(2) <= (others => '0');  -- RO
            registers(3) <= (others => '0');  -- RF
        elsif rising_edge(clk) then
            if we = '1' then
                registers(to_integer(unsigned(sel_rd))) <= data_in;
            end if;
        end if;
    end process;

    -- Asynchronous read (combinational)
    rs1_out <= registers(to_integer(unsigned(sel_rs1)));
    rs2_out <= registers(to_integer(unsigned(sel_rs2)));

    -- RO always output for 7-segment display
    ro_out <= registers(2);

    -- RF always output for branch conditions
    rf_out <= registers(3);

end Behavioral;

// VHDL entity program_counter, as the project stores it:
-- EE8 CPU Program Counter
-- 8-bit PC with jump/branch logic

library IEEE;
use IEEE.STD_LOGIC_1164.ALL;
use IEEE.NUMERIC_STD.ALL;

entity program_counter is
    Port (
        clk         : in  STD_LOGIC;                      -- Clock
        rst         : in  STD_LOGIC;                      -- Reset (sets PC to 0)
        halt        : in  STD_LOGIC;                      -- Halt signal (freezes PC)
        jump        : in  STD_LOGIC;                      -- Unconditional jump
        branch      : in  STD_LOGIC;                      -- Conditional branch
        branch_cond : in  STD_LOGIC;                      -- Branch condition (0=JZ, 1=JNZ)
        flag_rf     : in  STD_LOGIC_VECTOR(7 downto 0);   -- RF register for condition check
        jump_addr   : in  STD_LOGIC_VECTOR(7 downto 0);   -- Jump target address
        pc_out      : out STD_LOGIC_VECTOR(7 downto 0)    -- Current PC value
    );
end program_counter;

architecture Behavioral of program_counter is
    signal pc_reg : unsigned(7 downto 0);
    signal rf_is_zero : STD_LOGIC;
    signal branch_taken : STD_LOGIC;
begin

    -- Check if RF is zero
    rf_is_zero <= '1' when flag_rf = x"00" else '0';

    -- Determine if branch should be taken
    -- branch_cond=0: JZ (jump if zero) -> take if RF=0
    -- branch_cond=1: JNZ (jump if not zero) -> take if RF!=0
    branch_taken <= branch and ((not branch_cond and rf_is_zero) or
                                (branch_cond and not rf_is_zero));

    -- PC update logic
    process(clk, rst)
    begin
        if rst = '1' then
            pc_reg <= (others => '0');
        elsif rising_edge(clk) then
            if halt = '1' then
                -- PC unchanged on halt
                pc_reg <= pc_reg;
            elsif jump = '1' then
                -- Unconditional jump
                pc_reg <= unsigned(jump_addr);
            elsif branch_taken = '1' then
                -- Conditional branch taken
                pc_reg <= unsigned(jump_addr);
            else
                -- Normal increment
                pc_reg <= pc_reg + 1;
            end if;
        end if;
    end process;

    pc_out <= std_logic_vector(pc_reg);

end Behavioral;

// VHDL entity control_unit, as the project stores it:
-- EE8 CPU Control Unit
-- Generates control signals based on opcode

library IEEE;
use IEEE.STD_LOGIC_1164.ALL;

entity control_unit is
    Port (
        opcode      : in  STD_LOGIC_VECTOR(3 downto 0);   -- Instruction opcode
        reg_write   : out STD_LOGIC;                       -- Enable register write
        alu_op      : out STD_LOGIC_VECTOR(3 downto 0);   -- ALU operation
        imm_sel     : out STD_LOGIC;                       -- Select immediate (for LDI)
        jump        : out STD_LOGIC;                       -- Unconditional jump
        branch      : out STD_LOGIC;                       -- Conditional branch
        branch_cond : out STD_LOGIC;                       -- 0=JZ, 1=JNZ
        halt        : out STD_LOGIC;                       -- Halt CPU
        flag_write  : out STD_LOGIC                        -- Write to RF from flags
    );
end control_unit;

architecture Behavioral of control_unit is
begin
    process(opcode)
    begin
        -- Default values
        reg_write   <= '0';
        alu_op      <= "0000";
        imm_sel     <= '0';
        jump        <= '0';
        branch      <= '0';
        branch_cond <= '0';
        halt        <= '0';
        flag_write  <= '0';

        case opcode is
            -- ALU Operations (write result to Rd)
            when "0000" =>  -- ADD
                reg_write <= '1';
                alu_op <= "0000";

            when "0001" =>  -- SUB
                reg_write <= '1';
                alu_op <= "0001";

            when "0010" =>  -- AND
                reg_write <= '1';
                alu_op <= "0010";

            when "0011" =>  -- OR
                reg_write <= '1';
                alu_op <= "0011";

            when "0100" =>  -- XOR
                reg_write <= '1';
                alu_op <= "0100";

            when "0101" =>  -- SHL
                reg_write <= '1';
                alu_op <= "0101";

            when "0110" =>  -- SHR
                reg_write <= '1';
                alu_op <= "0110";

            when "0111" =>  -- MOV
                reg_write <= '1';
                alu_op <= "0111";

            -- Comparison Operations (write to RF)
            when "1000" =>  -- LT
                reg_write <= '1';
                flag_write <= '1';
                alu_op <= "1000";

            when "1001" =>  -- EQ
                reg_write <= '1';
                flag_write <= '1';
                alu_op <= "1001";

            -- Load Immediate
            when "1010" =>  -- LDI
                reg_write <= '1';
                imm_sel <= '1';
                alu_op <= "0111";  -- MOV (passthrough)

            -- Control Flow
            when "1011" =>  -- JMP (unconditional jump)
                jump <= '1';

            when "1100" =>  -- JZ (jump if RF=0)
                branch <= '1';
                branch_cond <= '0';

            when "1101" =>  -- JNZ (jump if RF!=0)
                branch <= '1';
                branch_cond <= '1';

            -- Reserved / NOP
            when "1110" =>  -- NOP
                null;  -- Do nothing

            -- Halt
            when "1111" =>  -- HALT
                halt <= '1';

            when others =>
                null;  -- Default: NOP behavior
        end case;
    end process;

end Behavioral;
