// Logisim project ROM.circ as structural Verilog: 1 circuit, main circuit ROM_TEST
module ROM_TEST (
  output [15:0] Instruction_1,
  output [15:0] Instruction_2,
  output [15:0] Instruction_3,
  output [15:0] Instruction_4,
  output [15:0] Instruction_5,
  output [15:0] Instruction_6,
  output [15:0] Instruction_7,
  output [15:0] Instruction_8,
  output [15:0] Instruction_9,
  output [15:0] Instruction_10,
  output [15:0] Instruction_11,
  output [15:0] Instruction_12,
  output [15:0] Instruction_13,
  output [15:0] Instruction_14,
  output [15:0] Instruction_15,
  output [15:0] Instruction_16
);

  LED led_1 (.in(1'b1));
  LED led_2 (.in(1'b1));
  LED led_3 (.in(1'b1));
  LED led_4 (.in(1'b0));
  LED led_5 (.in(1'b1));
  LED led_6 (.in(1'b1));
  LED led_7 (.in(1'b1));
  LED led_8 (.in(1'b0));
  LED led_9 (.in(1'b1));
  LED led_10 (.in(1'b1));
  LED led_11 (.in(1'b1));
  LED led_12 (.in(1'b1));
  LED led_13 (.in(1'b1));
  LED led_14 (.in(1'b1));
  LED led_15 (.in(1'b1));
  LED led_16 (.in(1'b1));
  LED led_17 (.in(1'b0));
  LED led_18 (.in(1'b1));
  LED led_19 (.in(1'b0));
  LED led_20 (.in(1'b1));
  LED led_21 (.in(1'b0));
  LED led_22 (.in(1'b1));
  LED led_23 (.in(1'b0));
  LED led_24 (.in(1'b0));
  LED led_25 (.in(1'b0));
  LED led_26 (.in(1'b0));
  LED led_27 (.in(1'b1));
  LED led_28 (.in(1'b1));
  LED led_29 (.in(1'b1));
  LED led_30 (.in(1'b0));
  LED led_31 (.in(1'b0));
  LED led_32 (.in(1'b0));
  LED led_33 (.in(1'b1));
  LED led_34 (.in(1'b0));
  LED led_35 (.in(1'b0));
  LED led_36 (.in(1'b0));
  LED led_37 (.in(1'b0));
  LED led_38 (.in(1'b1));
  LED led_39 (.in(1'b1));
  LED led_40 (.in(1'b0));
  LED led_41 (.in(1'b1));
  LED led_42 (.in(1'b0));
  LED led_43 (.in(1'b1));
  LED led_44 (.in(1'b1));
  LED led_45 (.in(1'b1));
  LED led_46 (.in(1'b1));
  LED led_47 (.in(1'b1));
  LED led_48 (.in(1'b1));
  LED led_49 (.in(1'b0));
  LED led_50 (.in(1'b1));
  LED led_51 (.in(1'b0));
  LED led_52 (.in(1'b0));
  LED led_53 (.in(1'b0));
  LED led_54 (.in(1'b0));
  LED led_55 (.in(1'b1));
  LED led_56 (.in(1'b0));
  LED led_57 (.in(1'b1));
  LED led_58 (.in(1'b1));
  LED led_59 (.in(1'b0));
  LED led_60 (.in(1'b0));
  LED led_61 (.in(1'b1));
  LED led_62 (.in(1'b0));
  LED led_63 (.in(1'b1));
  LED led_64 (.in(1'b0));
  LED led_65 (.in(1'b0));
  LED led_66 (.in(1'b1));
  LED led_67 (.in(1'b1));
  LED led_68 (.in(1'b1));
  LED led_69 (.in(1'b1));
  LED led_70 (.in(1'b0));
  LED led_71 (.in(1'b1));
  LED led_72 (.in(1'b0));
  LED led_73 (.in(1'b1));
  LED led_74 (.in(1'b0));
  LED led_75 (.in(1'b0));
  LED led_76 (.in(1'b0));
  LED led_77 (.in(1'b0));
  LED led_78 (.in(1'b0));
  LED led_79 (.in(1'b0));
  LED led_80 (.in(1'b1));
  LED led_81 (.in(1'b0));
  LED led_82 (.in(1'b0));
  LED led_83 (.in(1'b0));
  LED led_84 (.in(1'b0));
  LED led_85 (.in(1'b1));
  LED led_86 (.in(1'b0));
  LED led_87 (.in(1'b0));
  LED led_88 (.in(1'b0));
  LED led_89 (.in(1'b0));
  LED led_90 (.in(1'b0));
  LED led_91 (.in(1'b0));
  LED led_92 (.in(1'b0));
  LED led_93 (.in(1'b0));
  LED led_94 (.in(1'b0));
  LED led_95 (.in(1'b0));
  LED led_96 (.in(1'b0));
  LED led_97 (.in(1'b0));
  LED led_98 (.in(1'b1));
  LED led_99 (.in(1'b1));
  LED led_100 (.in(1'b0));
  LED led_101 (.in(1'b0));
  LED led_102 (.in(1'b0));
  LED led_103 (.in(1'b0));
  LED led_104 (.in(1'b0));
  LED led_105 (.in(1'b0));
  LED led_106 (.in(1'b0));
  LED led_107 (.in(1'b0));
  LED led_108 (.in(1'b0));
  LED led_109 (.in(1'b0));
  LED led_110 (.in(1'b0));
  LED led_111 (.in(1'b0));
  LED led_112 (.in(1'b0));
  LED led_113 (.in(1'b0));
  LED led_114 (.in(1'b0));
  LED led_115 (.in(1'b0));
  LED led_116 (.in(1'b0));
  LED led_117 (.in(1'b0));
  LED led_118 (.in(1'b0));
  LED led_119 (.in(1'b1));
  LED led_120 (.in(1'b0));
  LED led_121 (.in(1'b0));
  LED led_122 (.in(1'b1));
  LED led_123 (.in(1'b0));
  LED led_124 (.in(1'b0));
  LED led_125 (.in(1'b0));
  LED led_126 (.in(1'b0));
  LED led_127 (.in(1'b1));
  LED led_128 (.in(1'b0));
  LED led_129 (.in(1'b0));
  LED led_130 (.in(1'b0));
  LED led_131 (.in(1'b1));
  LED led_132 (.in(1'b0));
  LED led_133 (.in(1'b0));
  LED led_134 (.in(1'b0));
  LED led_135 (.in(1'b0));
  LED led_136 (.in(1'b0));
  LED led_137 (.in(1'b0));
  LED led_138 (.in(1'b1));
  LED led_139 (.in(1'b0));
  LED led_140 (.in(1'b0));
  LED led_141 (.in(1'b0));
  LED led_142 (.in(1'b0));
  LED led_143 (.in(1'b0));
  LED led_144 (.in(1'b0));
  LED led_145 (.in(1'b0));
  LED led_146 (.in(1'b0));
  LED led_147 (.in(1'b0));
  LED led_148 (.in(1'b0));
  LED led_149 (.in(1'b0));
  LED led_150 (.in(1'b0));
  LED led_151 (.in(1'b0));
  LED led_152 (.in(1'b0));
  LED led_153 (.in(1'b0));
  LED led_154 (.in(1'b0));
  LED led_155 (.in(1'b0));
  LED led_156 (.in(1'b0));
  LED led_157 (.in(1'b0));
  LED led_158 (.in(1'b0));
  LED led_159 (.in(1'b0));
  LED led_160 (.in(1'b0));
  LED led_161 (.in(1'b0));
  LED led_162 (.in(1'b0));
  LED led_163 (.in(1'b0));
  LED led_164 (.in(1'b0));
  LED led_165 (.in(1'b0));
  LED led_166 (.in(1'b0));
  LED led_167 (.in(1'b0));
  LED led_168 (.in(1'b0));
  LED led_169 (.in(1'b1));
  LED led_170 (.in(1'b1));
  LED led_171 (.in(1'b0));
  LED led_172 (.in(1'b0));
  LED led_173 (.in(1'b0));
  LED led_174 (.in(1'b0));
  LED led_175 (.in(1'b0));
  LED led_176 (.in(1'b0));
  LED led_177 (.in(1'b0));
  LED led_178 (.in(1'b0));
  LED led_179 (.in(1'b0));
  LED led_180 (.in(1'b0));
  LED led_181 (.in(1'b1));
  LED led_182 (.in(1'b0));
  LED led_183 (.in(1'b0));
  LED led_184 (.in(1'b0));
  LED led_185 (.in(1'b0));
  LED led_186 (.in(1'b0));
  LED led_187 (.in(1'b0));
  LED led_188 (.in(1'b0));
  LED led_189 (.in(1'b0));
  LED led_190 (.in(1'b0));
  LED led_191 (.in(1'b0));
  LED led_192 (.in(1'b0));
  LED led_193 (.in(1'b0));
  LED led_194 (.in(1'b0));
  LED led_195 (.in(1'b0));
  LED led_196 (.in(1'b0));
  LED led_197 (.in(1'b0));
  LED led_198 (.in(1'b1));
  LED led_199 (.in(1'b0));
  LED led_200 (.in(1'b0));
  LED led_201 (.in(1'b1));
  LED led_202 (.in(1'b1));
  LED led_203 (.in(1'b0));
  LED led_204 (.in(1'b0));
  LED led_205 (.in(1'b0));
  LED led_206 (.in(1'b0));
  LED led_207 (.in(1'b0));
  LED led_208 (.in(1'b0));
  LED led_209 (.in(1'b0));
  LED led_210 (.in(1'b0));
  LED led_211 (.in(1'b0));
  LED led_212 (.in(1'b0));
  LED led_213 (.in(1'b0));
  LED led_214 (.in(1'b1));
  LED led_215 (.in(1'b0));
  LED led_216 (.in(1'b0));
  LED led_217 (.in(1'b0));
  LED led_218 (.in(1'b0));
  LED led_219 (.in(1'b1));
  LED led_220 (.in(1'b1));
  LED led_221 (.in(1'b1));
  LED led_222 (.in(1'b0));
  LED led_223 (.in(1'b0));
  LED led_224 (.in(1'b0));
  LED led_225 (.in(1'b0));
  LED led_226 (.in(1'b0));
  LED led_227 (.in(1'b0));
  LED led_228 (.in(1'b0));
  LED led_229 (.in(1'b1));
  LED led_230 (.in(1'b0));
  LED led_231 (.in(1'b1));
  LED led_232 (.in(1'b1));
  LED led_233 (.in(1'b1));
  LED led_234 (.in(1'b1));
  LED led_235 (.in(1'b0));
  LED led_236 (.in(1'b0));
  LED led_237 (.in(1'b0));
  LED led_238 (.in(1'b0));
  LED led_239 (.in(1'b0));
  LED led_240 (.in(1'b0));
  LED led_241 (.in(1'b0));
  LED led_242 (.in(1'b1));
  LED led_243 (.in(1'b0));
  LED led_244 (.in(1'b0));
  LED led_245 (.in(1'b0));
  LED led_246 (.in(1'b1));
  LED led_247 (.in(1'b1));
  LED led_248 (.in(1'b0));
  LED led_249 (.in(1'b0));
  LED led_250 (.in(1'b0));
  LED led_251 (.in(1'b0));
  LED led_252 (.in(1'b1));
  LED led_253 (.in(1'b1));
  LED led_254 (.in(1'b0));
  LED led_255 (.in(1'b0));
  LED led_256 (.in(1'b0));

  assign Instruction_1 = 16'ha800;
  assign Instruction_2 = 16'ha001;
  assign Instruction_3 = 16'ha40a;
  assign Instruction_4 = 16'h880;
  assign Instruction_5 = 16'h9900;
  assign Instruction_6 = 16'he007;
  assign Instruction_7 = 16'hb003;
  assign Instruction_8 = 16'h880;
  assign Instruction_9 = 16'hac00;
  assign Instruction_10 = 16'h9b00;
  assign Instruction_11 = 16'hd00c;
  assign Instruction_12 = 16'hb007;
  assign Instruction_13 = 16'ha8ff;
  assign Instruction_14 = 16'he000;
  assign Instruction_15 = 16'he000;
  assign Instruction_16 = 16'hf000;

  // Notes on the sheet:
  //   NOOP
  //   NOOP
  //   HALT
  //   Sleep for 2 cycles, then HALT
  //   Documentation:
  //   LDI RO, 0
  //   LDI R0, 1
  //   LDI R1, 10
  //   ADD RO, R0, RO
  //   EQ RO, R1
  //   JNZ 7
  //   JMP 3
  //   SUB RO, R0, RO
  //   LDI RF, 0
  //   EQ RO, RF
  //   JNZ 12
  //   JMP 7
  //   LDI R0, 0xFF
  //   And in human language;
  //   Count up to 10, then count down to 0.
  //   Once done, put 1111 1111 to the out register (FF in hex)
  //   A40A
  //   9900
  //   B003
  //   AC00
  //   D00C
  //   B007
  //   E000
  //   A800
  //   1010 1000 0000 0000
  //   A001
  //   1010 0000 0000 0001
  //   1010 0100 0000 1010
  //   0880
  //   0000 1000 1000 0000
  //   1001 1001 0000 0000
  //   D007
  //   1110 0000 0000 0111
  //   1011 0000 0000 0011
  //   1880
  //   0000 1000 1000 0000
  //   1010 1100 0000 0000
  //   9B00
  //   1001 1011 0000 0000
  //   1101 0000 0000 1100
  //   1011 0000 0000 0111
  //   A8FF
  //   1010 1000 1111 1111
  //   1110 0000 0000 0000
  //   E000
  //   1110 0000 0000 0000
  //   F000
  //   1111 0000 0000 0000
  //   LDI R0, 1
  //   LDI R1, 10
  //   ADD RO, R0, RO
  //   EQ RO, R1
  //   JNZ 7
  //   JMP 3
  //   SUB RO, R0, RO
  //   LDI RF, 0
  //   EQ RO, RF
  //   JNZ 12
  //   JMP 7
  //   LDI R0, 0xFF
  //   NOOP
  //   NOOP
  //   HALT
  //   LDI RO, 0
endmodule
