// Logisim project ee8_cpu.circ as structural Verilog: 8 circuits, main circuit main
// DECODE
module InstructionDecoder (
  input  [15:0] instruction,
  output [1:0] rd,
  output [1:0] rs2,
  output [1:0] rs1,
  output [7:0] immediate,
  output [3:0] opcode
);


  assign immediate = instruction[7:0];
  assign opcode = instruction[15:12];
  assign rd = instruction[7:6];
  assign rs1 = instruction[11:10];
  assign rs2 = instruction[9:8];

  // Notes on the sheet:
  //   INPUT: 16-bit instruction
  //   16-bit splitter
  //   WIRING: Connect splitter outputs to combiners:
  //   bit15,14,13,12 -> opcode combiner
  //   bit11,10 -> rs1 combiner
  //   bit9,8 -> rs2 combiner
  //   bit7,6 -> rd combiner
  //   bit7,6,5,4,3,2,1,0 -> immediate combiner
  //   === WIRING GUIDE ===
  //   instruction (16-bit) -> 16-bit SPLITTER input
  //   SPLITTER bit 15 -> OPCODE_COMBINER bit 3
  //   SPLITTER bit 14 -> OPCODE_COMBINER bit 2
  //   SPLITTER bit 13 -> OPCODE_COMBINER bit 1
  //   SPLITTER bit 12 -> OPCODE_COMBINER bit 0
  //   OPCODE_COMBINER output -> opcode (4-bit)
  //   SPLITTER bit 11 -> RS1_COMBINER bit 1
  //   SPLITTER bit 10 -> RS1_COMBINER bit 0
  //   RS1_COMBINER output -> rs1 (2-bit)
  //   SPLITTER bit 9 -> RS2_COMBINER bit 1
  //   SPLITTER bit 8 -> RS2_COMBINER bit 0
  //   RS2_COMBINER output -> rs2 (2-bit)
  //   SPLITTER bit 7 -> RD_COMBINER bit 1, IMM_COMBINER bit 7
  //   SPLITTER bit 6 -> RD_COMBINER bit 0, IMM_COMBINER bit 6
  //   RD_COMBINER output -> rd (2-bit)
  //   SPLITTER bits 5,4,3,2,1,0 -> IMM_COMBINER bits 5,4,3,2,1,0
  //   IMM_COMBINER output -> immediate (8-bit)
  //   INSTRUCTION DECODER
  //   Extracts fields from 16-bit instruction
  //   bits [15:12] -> opcode (4-bit)
  //   bits [7:0] -> immediate (8-bit)
  //   bits [7:6] -> rd (2-bit)
  //   bits [9:8] -> rs2 (2-bit)
  //   bits [11:10] -> rs1 (2-bit)
endmodule

// CTRL
module ControlUnit (
  input  [3:0] opcode,
  output flag_write,
  output halt,
  output branch_cond,
  output branch,
  output jump,
  output imm_sel,
  output reg_write,
  output [3:0] alu_op
);

  wire [0:0] rom_1_data;

  ROM_part #(.addrWidth(4), .dataWidth(12)) rom_1 (
    .addr(opcode),
    .data({alu_op, reg_write, imm_sel, jump, branch, branch_cond, halt, flag_write, rom_1_data[0]}));

  // Notes on the sheet:
  //   INPUT: 4-bit opcode
  //   === WIRING GUIDE ===
  //   opcode (4-bit) -> CONTROL_ROM address input
  //   CONTROL_ROM data output (12-bit) -> 12-bit SPLITTER input
  //   SPLITTER bit 11 -> ALU_OP_COMBINER bit 3
  //   SPLITTER bit 10 -> ALU_OP_COMBINER bit 2
  //   SPLITTER bit 9 -> ALU_OP_COMBINER bit 1
  //   SPLITTER bit 8 -> ALU_OP_COMBINER bit 0
  //   ALU_OP_COMBINER output -> alu_op (4-bit)
  //   SPLITTER bit 7 -> reg_write
  //   SPLITTER bit 6 -> imm_sel
  //   SPLITTER bit 5 -> jump
  //   SPLITTER bit 4 -> branch
  //   SPLITTER bit 3 -> branch_cond
  //   SPLITTER bit 2 -> halt
  //   SPLITTER bit 1 -> flag_write
  //   (SPLITTER bit 0 is unused)
  //   Control ROM: 16x12 bits
  //   CONTROL UNIT (ROM-based)
  //   contents of rom_1 (hex, n*v repeats v):
  //   80 180 280 380 480 580 680 780 882 982 7c0 20 10 18 0 4
  //   ROM ENCODING:
  //   0=ADD  1=SUB  2=AND  3=OR   4=XOR
  //   5=SHL  6=SHR  7=MOV  8=LT   9=EQ
  //   A=LDI  B=JMP  C=JZ   D=JNZ  E=NOP  F=HALT
  //   OUTPUTS:
  //   bits[11:8] -> alu_op (4-bit)
  //   bit[1] -> flag_write
  //   bit[2] -> halt
  //   bit[3] -> branch_cond
  //   bit[4] -> branch
  //   bit[5] -> jump
  //   bit[6] -> imm_sel
  //   bit[7] -> reg_write
endmodule

module ALU (
  input  [7:0] A,
  input  [7:0] B,
  input  [3:0] alu_op,
  output [7:0] result,
  output flag_eq,
  output flag_lt
);

  wire [7:0] adder_1_out, and_1_out, multiplexer_1_out, multiplexer_2_out, or_1_out, shifter_1_out,
       shifter_2_out, subtractor_1_out, xor_1_out;

  Adder adder_1 (.a(A), .b(B), .out(adder_1_out));  // open: cin, cout
  Subtractor subtractor_1 (.a(A), .b(B), .out(subtractor_1_out));  // open: bin, bout
  assign and_1_out = A & B;  // AND_Gate and_1, 8 bits wide
  assign or_1_out = A | B;  // OR_Gate or_1, 8 bits wide
  assign xor_1_out = A ^ B;  // XOR_Gate xor_1, 8 bits wide
  Shifter shifter_1 (.in(A), .\dist (B[2:0]), .out(shifter_1_out));
  Shifter #(.shift("lr")) shifter_2 (.in(A), .\dist (B[2:0]), .out(shifter_2_out));
  Comparator comparator_1 (.a(A), .b(B), .eq(flag_eq), .lt(flag_lt));  // open: gt
  Multiplexer #(.width(8)) multiplexer_1 (.in0({8{1'b0}}), .in1(8'h1), .out(multiplexer_1_out), .sel(flag_lt));
  Multiplexer #(.width(8)) multiplexer_2 (.in0({8{1'b0}}), .in1(8'h1), .out(multiplexer_2_out), .sel(flag_eq));
  Multiplexer #(.select(4), .width(8)) multiplexer_3 (
    .in0(adder_1_out), .in1(subtractor_1_out), .in2(and_1_out), .in3(or_1_out), .in4(xor_1_out),
    .in5(shifter_1_out), .in6(shifter_2_out), .in7(A), .in8(multiplexer_1_out), .in9(multiplexer_2_out),
    .in10({8{1'b0}}), .in11({8{1'b0}}), .in12({8{1'b0}}), .in13({8{1'b0}}), .in14({8{1'b0}}),
    .in15({8{1'b0}}), .out(result), .sel(alu_op));

  // Notes on the sheet:
  //   INPUT A (8-bit)
  //   INPUT B (8-bit)
  //   B[2:0] extractor for shift
  //   5: SHL (use B[2:0])
  //   use LT output
  //   9: EQ (A=B -> 0x01, else 0x00)
  //   use EQ output from same comparator
  //   0: ADD
  //   1: SUB
  //   2: AND
  //   3: OR
  //   4: XOR
  //   6: SHR (use B[2:0])
  //   7: MOV (just pass A through)
  //   8: LT (A<B -> 0x01, else 0x00)
  //   flag_eq (from comparator)
  //   8-BIT ALU
  //   LT MUX (sel=LT flag)
  //   0x00
  //   0x01
  //   EQ MUX (sel=EQ flag)
  //   flag_lt (from comparator)
  //   10-15: tie to 0
  //   alu_op (4-bit)
  //   RESULT MUX
  //   16-to-1, 8-bit
  //   sel = alu_op
  //   0:ADD
  //   1:SUB
  //   2:AND
  //   3:OR
  //   4:XOR
  //   5:SHL
  //   6:SHR
  //   7:MOV
  //   8:LT
  //   9:EQ
  //   OUTPUT: result (8-bit)
  //   === WIRING GUIDE ===
  //   A (8-bit) -> ADDER.A, SUBTRACTOR.A, AND.in1, OR.in1, XOR.in1
  //   A (8-bit) -> SHL_SHIFTER.data, SHR_SHIFTER.data, COMPARATOR.A
  //   A (8-bit) -> RESULT_MUX input 7 (for MOV passthrough)
  //   B (8-bit) -> ADDER.B, SUBTRACTOR.B, AND.in2, OR.in2, XOR.in2
  //   B (8-bit) -> COMPARATOR.B
  //   B[2:0] (3-bit via splitter) -> SHL_SHIFTER.dist, SHR_SHIFTER.dist
  //   alu_op (4-bit) -> RESULT_MUX sel
  //   ADDER.out -> RESULT_MUX input 0
  //   SUBTRACTOR.out -> RESULT_MUX input 1
  //   AND.out -> RESULT_MUX input 2
  //   OR.out -> RESULT_MUX input 3
  //   XOR.out -> RESULT_MUX input 4
  //   SHL_SHIFTER.out -> RESULT_MUX input 5
  //   SHR_SHIFTER.out -> RESULT_MUX input 6
  //   A -> RESULT_MUX input 7 (MOV)
  //   LT_MUX.out -> RESULT_MUX input 8
  //   EQ_MUX.out -> RESULT_MUX input 9
  //   0x00 constant -> RESULT_MUX inputs 10-15 (unused ops)
  //   RESULT_MUX.out -> result (8-bit output)
  //   LT/EQ COMPARISON LOGIC:
  //   COMPARATOR.LT_out -> LT_MUX.sel, flag_lt output
  //   COMPARATOR.EQ_out -> EQ_MUX.sel, flag_eq output
  //   0x00 constant -> LT_MUX input 0, EQ_MUX input 0
  //   0x01 constant -> LT_MUX input 1, EQ_MUX input 1
  //   (LT_MUX outputs 0x01 if A<B, else 0x00)
  //   (EQ_MUX outputs 0x01 if A=B, else 0x00)
endmodule

// REGS
module RegisterFile (
  input  clk,
  input  rst,
  input  [1:0] sel_rs1,
  input  we,
  input  [1:0] sel_rd,
  input  [1:0] sel_rs2,
  input  [7:0] data_in,
  output [7:0] rs1_out,
  output [7:0] rs2_out,
  output [7:0] ro_out,
  output [7:0] rf_out
);

  wire demultiplexer_1_out0, demultiplexer_1_out1, demultiplexer_1_out2, demultiplexer_1_out3;
  wire [7:0] register_1_q, register_2_q;

  Demultiplexer #(.select(2)) demultiplexer_1 (
    .out0(demultiplexer_1_out0), .out1(demultiplexer_1_out1), .out2(demultiplexer_1_out2),
    .out3(demultiplexer_1_out3), .in(we), .sel(sel_rd));
  Register register_1 (.D(data_in), .en(demultiplexer_1_out0), .clk(clk), .Q(register_1_q), .clr(rst));
  Register register_2 (.D(data_in), .en(demultiplexer_1_out1), .clk(clk), .Q(register_2_q), .clr(rst));
  Register register_3 (.D(data_in), .en(demultiplexer_1_out2), .clk(clk), .Q(ro_out), .clr(rst));
  Register register_4 (.D(data_in), .en(demultiplexer_1_out3), .clk(clk), .Q(rf_out), .clr(rst));
  Multiplexer #(.select(2), .width(8)) multiplexer_1 (
    .in0(register_1_q), .in1(register_2_q), .in2(ro_out), .in3(rf_out), .out(rs1_out), .sel(sel_rs1));
  Multiplexer #(.select(2), .width(8)) multiplexer_2 (
    .in0(register_1_q), .in1(register_2_q), .in2(ro_out), .in3(rf_out), .out(rs2_out), .sel(sel_rs2));

  // Notes on the sheet:
  //   clk
  //   rst (async)
  //   we (write enable)
  //   sel_rd (2-bit)
  //   data_in (8-bit)
  //   === WIRING GUIDE ===
  //   clk -> R0.clk, R1.clk, RO.clk, RF.clk
  //   rst -> R0.clr, R1.clr, RO.clr, RF.clr
  //   data_in (8-bit) -> R0.D, R1.D, RO.D, RF.D
  //   we -> WRITE_DEMUX input
  //   sel_rd (2-bit) -> WRITE_DEMUX sel
  //   WRITE_DEMUX output 0 -> R0.en
  //   WRITE_DEMUX output 1 -> R1.en
  //   WRITE_DEMUX output 2 -> RO.en
  //   WRITE_DEMUX output 3 -> RF.en
  //   R0.Q -> RS1_MUX input 0, RS2_MUX input 0
  //   R1.Q -> RS1_MUX input 1, RS2_MUX input 1
  //   RO.Q -> RS1_MUX input 2, RS2_MUX input 2, ro_out
  //   RF.Q -> RS1_MUX input 3, RS2_MUX input 3, rf_out
  //   sel_rs1 (2-bit) -> RS1_MUX sel
  //   RS1_MUX output -> rs1_out
  //   sel_rs2 (2-bit) -> RS2_MUX sel
  //   RS2_MUX output -> rs2_out
  //   WRITE DEMUX
  //   in=we, sel=sel_rd
  //   R0 (en from demux[0])
  //   R1 (en from demux[1])
  //   RO (en from demux[2])
  //   RF (en from demux[3])
  //   REGISTER FILE (4x8-bit)
  //   R0=00, R1=01, RO=10, RF=11
  //   WIRING: data_in -> all reg inputs, clk -> all clk, rst -> all clr
  //   RS1 MUX
  //   sel=sel_rs1
  //   0:R0 1:R1 2:RO 3:RF
  //   sel_rs1 (2-bit)
  //   RS2 MUX
  //   sel=sel_rs2
  //   sel_rs2 (2-bit)
  //   RO always out (7-seg)
  //   RF always out (branch)
endmodule

// PC
module ProgramCounter (
  input  clk,
  input  rst,
  input  [7:0] jump_addr,
  input  halt,
  input  jump,
  input  branch,
  input  branch_cond,
  input  [7:0] flag_rf,
  output [7:0] pc_out
);

  wire and_1_out, and_2_out, and_3_out, comparator_1_eq, not_1_out, not_2_out, not_3_out, or_1_out, or_2_out;
  wire [7:0] adder_1_out, multiplexer_1_out;

  Register register_1 (.D(multiplexer_1_out), .en(not_1_out), .clk(clk), .Q(pc_out), .clr(rst));
  not not_1 (not_1_out, halt);
  not not_2 (not_2_out, comparator_1_eq);
  Comparator comparator_1 (.a(flag_rf), .b({8{1'b0}}), .eq(comparator_1_eq));  // open: gt, lt
  not not_3 (not_3_out, branch_cond);
  Adder adder_1 (.a(pc_out), .b(8'h1), .out(adder_1_out));  // open: cin, cout
  and and_1 (and_1_out, not_3_out, comparator_1_eq);
  and and_2 (and_2_out, branch_cond, not_2_out);
  or or_1 (or_1_out, and_1_out, and_2_out);
  Multiplexer #(.width(8)) multiplexer_1 (.in0(adder_1_out), .in1(jump_addr), .out(multiplexer_1_out), .sel(or_2_out));
  or or_2 (or_2_out, jump, and_3_out);
  and and_3 (and_3_out, branch, or_1_out);

  // Notes on the sheet:
  //   RF register value
  //   NOT halt -> write enable
  //   0=JZ, 1=JNZ
  //   PC REGISTER
  //   EQ out = rf_is_zero
  //   RF == 0 ?
  //   NOT branch_cond
  //   NOT rf_is_zero
  //   PC + 1
  //   immediate field
  //   JZ_taken
  //   PROGRAM COUNTER
  //   JNZ_taken
  //   Captain Picard, execute the jump
  //   Any jump taken
  //   NEXT PC MUX
  //   0=PC+1, 1=jump_addr
  //   sel=take_jump
  //   take_jump (to MUX sel)
  //   branch_taken
  //   OUTPUT: pc_out
  //   (feedback to adder input)
  //   BRANCH LOGIC:
  //   JZ_taken = (branch_cond==0) AND rf_is_zero
  //   JNZ_taken = (branch_cond==1) AND NOT rf_is_zero
  //   branch_taken = branch AND (JZ_taken OR JNZ_taken)
  //   take_jump = jump OR branch_taken
  //   === WIRING GUIDE ===
  //   clk -> PC_REGISTER.clk
  //   rst -> PC_REGISTER.clr
  //   halt -> NOT gate -> NOT_halt -> PC_REGISTER.en
  //   flag_rf -> Comparator.A, 0x00 const -> Comparator.B
  //   Comparator.EQ_out = rf_is_zero
  //   branch_cond -> NOT gate -> NOT_branch_cond
  //   rf_is_zero -> NOT gate -> NOT_rf_is_zero
  //   NOT_branch_cond AND rf_is_zero -> JZ_taken
  //   branch_cond AND NOT_rf_is_zero -> JNZ_taken
  //   JZ_taken OR JNZ_taken -> OR gate output
  //   branch AND (JZ_taken OR JNZ_taken) -> branch_taken
  //   jump OR branch_taken -> take_jump (MUX sel)
  //   PC_REGISTER.out (feedback) -> Adder.A
  //   0x01 constant -> Adder.B
  //   Adder.out (PC+1) -> NEXT_PC_MUX input 0
  //   jump_addr -> NEXT_PC_MUX input 1
  //   take_jump -> NEXT_PC_MUX.sel
  //   NEXT_PC_MUX.out -> PC_REGISTER.D
  //   PC_REGISTER.Q -> pc_out
endmodule

module ROM (
  input  [7:0] addr,
  output [15:0] data
);

  ROM_part #(.dataWidth(16)) rom_1 (.addr(addr), .data(data));

  // Notes on the sheet:
  //   addr (8-bit) from PC
  //   TEST PROGRAM:
  //   0: A00A = LDI R0, 10
  //   1: A405 = LDI R1, 5
  //   2: 0180 = ADD R0, R1, RO
  //   3: F000 = HALT
  //   Expected: RO = 0x0F (15)
  //   PROGRAM ROM (256 x 16-bit)
  //   contents of rom_1 (hex, n*v repeats v):
  //   0 a00a a405 180 f000 4 12*e000 10 16*e000 20 16*e000 30 16*e000 40 16*e000 50 16*e000 60 16*e000 70
  //   16*e000 80 16*e000 90 16*e000 a0 16*e000 b0 16*e000 c0 16*e000 d0 16*e000 e0 16*e000
  //   data (16-bit instruction)
endmodule

// CPU
module EE8_CPU (
  input  clk,
  input  rst,
  output [7:0] rom_addr,
  output [7:0] seven_seg
);

  wire controlunit_1_branch, controlunit_1_branch_cond, controlunit_1_halt, controlunit_1_jump,
       controlunit_1_reg_write;
  wire [1:0] controlunit_1_imm_sel, instructiondecoder_1_rd, instructiondecoder_1_rs1,
       instructiondecoder_1_rs2, multiplexer_2_out;
  wire [3:0] controlunit_1_alu_op, instructiondecoder_1_opcode;
  wire [7:0] alu_1_result, instructiondecoder_1_immediate, multiplexer_1_out, registerfile_1_rf_out,
       registerfile_1_rs1_out, registerfile_1_rs2_out;
  wire [15:0] rom_1_data;

  ProgramCounter programcounter_1 (
    .clk(clk), .rst(rst), .jump_addr(instructiondecoder_1_immediate), .halt(controlunit_1_halt),
    .jump(controlunit_1_jump), .branch(controlunit_1_branch), .branch_cond(controlunit_1_branch_cond),
    .flag_rf(registerfile_1_rf_out), .pc_out(rom_addr));
  RegisterFile registerfile_1 (
    .clk(clk), .rst(rst), .sel_rs1(instructiondecoder_1_rs1), .we(controlunit_1_reg_write),
    .sel_rd(multiplexer_2_out), .sel_rs2(instructiondecoder_1_rs2), .data_in(alu_1_result),
    .rs1_out(registerfile_1_rs1_out), .rs2_out(registerfile_1_rs2_out), .ro_out(seven_seg),
    .rf_out(registerfile_1_rf_out));
  InstructionDecoder instructiondecoder_1 (
    .instruction(rom_1_data), .rd(instructiondecoder_1_rd), .rs2(instructiondecoder_1_rs2),
    .rs1(instructiondecoder_1_rs1), .immediate(instructiondecoder_1_immediate),
    .opcode(instructiondecoder_1_opcode));
  Multiplexer #(.width(8)) multiplexer_1 (
    .in0(registerfile_1_rs1_out), .in1(instructiondecoder_1_immediate), .out(multiplexer_1_out),
    .sel(controlunit_1_imm_sel[0]));
  Multiplexer #(.select(2), .width(2)) multiplexer_2 (
    .in0(instructiondecoder_1_rd), .in1(instructiondecoder_1_rs1), .in2(2'b11), .in3(2'b00),
    .out(multiplexer_2_out), .sel(controlunit_1_imm_sel));
  ROM rom_1 (.addr(rom_addr), .data(rom_1_data));
  ControlUnit controlunit_1 (
    .opcode(instructiondecoder_1_opcode), .flag_write(controlunit_1_imm_sel[1]), .halt(controlunit_1_halt),
    .branch_cond(controlunit_1_branch_cond), .branch(controlunit_1_branch), .jump(controlunit_1_jump),
    .imm_sel(controlunit_1_imm_sel[0]), .reg_write(controlunit_1_reg_write), .alu_op(controlunit_1_alu_op));
  ALU alu_1 (
    .A(multiplexer_1_out), .B(registerfile_1_rs2_out), .alu_op(controlunit_1_alu_op), .result(alu_1_result));  // open: flag_eq, flag_lt

  // Notes on the sheet:
  //   EXTERNAL: clk
  //   EXTERNAL: rst
  //   PC
  //   REGISTERS
  //   EE8 CPU - TOP LEVEL INTEGRATION
  //   Wire the subcircuits according to the connection guide below
  //   DECODER
  //   RF=11
  //   CONTROL.alu_op -> ALU.alu_op
  //   CONTROL.reg_write -> REGS.we
  //   CONTROL.imm_sel -> ALU_A_MUX sel, RD_SEL_MUX sel[0]
  //   CONTROL.flag_write -> RD_SEL_MUX sel[1]
  //   CONTROL.jump -> PC.jump
  //   CONTROL.branch -> PC.branch
  //   CONTROL.branch_cond -> PC.branch_cond
  //   CONTROL.halt -> PC.halt
  //   RD_SEL MUX
  //   0=rd 1=rs1 2=RF(11) 3=0
  //   ALU
  //   ROM
  //   ALU_A MUX
  //   0=rs1, 1=imm
  //   === CONNECTION GUIDE ===
  //   PC.pc_out -> ROM.addr, rom_addr output
  //   ROM.data -> DECODER.instruction
  //   DECODER.opcode -> CONTROL.opcode
  //   DECODER.rs1 -> REGS.sel_rs1
  //   DECODER.rs2 -> REGS.sel_rs2
  //   DECODER.rd -> RD_SEL_MUX input 0
  //   DECODER.rs1 -> RD_SEL_MUX input 1 (for LDI)
  //   DECODER.immediate -> ALU_A_MUX input 1, PC.jump_addr
  //   REGS.rs1_out -> ALU_A_MUX input 0
  //   REGS.rs2_out -> ALU.B
  //   REGS.rf_out -> PC.flag_rf
  //   REGS.ro_out -> seven_seg output
  //   ALU_A_MUX.out -> ALU.A
  //   ALU.result -> REGS.data_in
  //   RD_SEL_MUX.out -> REGS.sel_rd
  //   clk -> REGS.clk, PC.clk
  //   rst -> REGS.rst, PC.rst
  //   sel[0]=imm_sel, sel[1]=flag_write
  //   CONTROL
  //   rom_addr = PC output
  //   seven_seg = RO output
endmodule

module main (
  input  RESET
);

  wire CLK_out;
  wire [7:0] ee8_cpu_1_rom_addr, ee8_cpu_1_seven_seg;

  Clock CLK (.out(CLK_out));
  EE8_CPU ee8_cpu_1 (.clk(CLK_out), .rst(RESET), .rom_addr(ee8_cpu_1_rom_addr), .seven_seg(ee8_cpu_1_seven_seg));
  Hex_Digit_Display hex_digit_display_1 (.value(ee8_cpu_1_seven_seg[7:4]));  // open: dp
  Hex_Digit_Display hex_digit_display_2 (.value(ee8_cpu_1_rom_addr[7:4]));  // open: dp
  Hex_Digit_Display hex_digit_display_3 (.value(ee8_cpu_1_rom_addr[3:0]));  // open: dp
  Hex_Digit_Display hex_digit_display_4 (.value(ee8_cpu_1_seven_seg[3:0]));  // open: dp

  // Notes on the sheet:
  //   Clock (click to toggle)
  //   Reset (click to toggle)
  //   EE8 CPU
  //   EE8 CPU TEST BENCH
  //   INSTRUCTIONS:
  //   1. Click RESET once to initialize
  //   2. Click RESET again to release
  //   3. Use Ctrl+K to tick clock, or click CLK
  //   4. After 4 clocks: RO should show 0F
  //   PC splitter [7:4][3:0]
  //   RO High
  //   RO splitter [7:4][3:0]
  //   PC High
  //   PC Low
  //   RO Low
endmodule
