// Logisim project ee8_cpu_v4.circ as structural Verilog: 11 circuits, main circuit main
// DECODE
module InstructionDecoder (
  input  [15:0] instruction,
  output [1:0] rd,
  output [1:0] rs2,
  output [1:0] rs1,
  output [7:0] immediate,
  output [3:0] opcode,
  output [3:0] address
);


  assign address = instruction[3:0];
  assign immediate = instruction[7:0];
  assign opcode = instruction[15:12];
  assign rd = instruction[7:6];
  assign rs1 = instruction[11:10];
  assign rs2 = instruction[9:8];

  // Notes on the sheet:
  //   INPUT: 16-bit instruction
  //   16-bit splitter
  //   INSTRUCTION DECODER
  //   Extracts fields from 16-bit instruction
  //   v4.0: rs1 also serves as Rcond for JZ/JNZ
  //   v4.0: changed encoding from 9:8 to 11:10 for LDI
  //   bits [15:12] -> opcode (4-bit)
  //   bits [7:0] -> immediate (8-bit)
  //   bits [7:6] -> rd (2-bit)
  //   bits [9:8] -> rs2 (2-bit)
  //   bits [3:0] -> address (4-bit) for J-type
  //   bits [11:10] -> rs1 (2-bit) = Rcond for J-type
endmodule

// CTRL
module ControlUnit (
  input  [3:0] opcode,
  output mov_group,
  output flag_write,
  output halt,
  output branch_cond,
  output branch,
  output jump,
  output imm_sel,
  output reg_write,
  output [3:0] alu_op
);

  ROM_part #(.addrWidth(4), .dataWidth(12)) rom_1 (
    .addr(opcode), .data({alu_op, reg_write, imm_sel, jump, branch, branch_cond, halt, flag_write, mov_group}));

  // Notes on the sheet:
  //   INPUT: 4-bit opcode
  //   Control ROM: 16x12 bits
  //   CONTROL UNIT (ROM-based)
  //   contents of rom_1 (hex, n*v repeats v):
  //   80 180 280 380 480 580 680 781 882 982 7c0 20 10 18 0 4
  //   ROM ENCODING:
  //   0=ADD  1=SUB  2=AND  3=OR   4=XOR
  //   5=SHL  6=SHR  7=MOV  8=LT   9=EQ
  //   A=LDI  B=JMP  C=JZ   D=JNZ  E=RSVD  F=HALT
  //   v4.0: bit[0]=mov_group for IN/OUT disambig
  //   Opcode E=RESERVED (triggers SYS_ERR externally)
  //   OUTPUTS:
  //   bits[11:8] -> alu_op (4-bit)
  //   bit[0] -> mov_group (opcode=0111)
  //   bit[1] -> flag_write
  //   bit[2] -> halt
  //   bit[3] -> branch_cond
  //   bit[4] -> branch
  //   bit[5] -> jump
  //   bit[6] -> imm_sel
  //   bit[7] -> reg_write
endmodule

module ALU (
  input  [7:0] A,
  input  [7:0] B,
  input  [3:0] alu_op,
  output [7:0] result,
  output flag_eq,
  output flag_lt
);

  wire [7:0] adder_1_out, and_1_out, multiplexer_1_out, multiplexer_2_out, or_1_out, shifter_1_out,
       shifter_2_out, subtractor_1_out, xor_1_out;

  Adder adder_1 (.a(A), .b(B), .out(adder_1_out));  // open: cin, cout
  Subtractor subtractor_1 (.a(A), .b(B), .out(subtractor_1_out));  // open: bin, bout
  assign and_1_out = A & B;  // AND_Gate and_1, 8 bits wide
  assign or_1_out = A | B;  // OR_Gate or_1, 8 bits wide
  assign xor_1_out = A ^ B;  // XOR_Gate xor_1, 8 bits wide
  Shifter shifter_1 (.in(A), .\dist (B[2:0]), .out(shifter_1_out));
  Shifter #(.shift("lr")) shifter_2 (.in(A), .\dist (B[2:0]), .out(shifter_2_out));
  Comparator comparator_1 (.a(A), .b(B), .eq(flag_eq), .lt(flag_lt));  // open: gt
  Multiplexer #(.width(8)) multiplexer_1 (.in0({8{1'b0}}), .in1(8'h1), .out(multiplexer_1_out), .sel(flag_lt));
  Multiplexer #(.width(8)) multiplexer_2 (.in0({8{1'b0}}), .in1(8'h1), .out(multiplexer_2_out), .sel(flag_eq));
  Multiplexer #(.select(4), .width(8)) multiplexer_3 (
    .in0(adder_1_out), .in1(subtractor_1_out), .in2(and_1_out), .in3(or_1_out), .in4(xor_1_out),
    .in5(shifter_1_out), .in6(shifter_2_out), .in7(A), .in8(multiplexer_1_out), .in9(multiplexer_2_out),
    .in10({8{1'b0}}), .in11({8{1'b0}}), .in12({8{1'b0}}), .in13({8{1'b0}}), .in14({8{1'b0}}),
    .in15({8{1'b0}}), .out(result), .sel(alu_op));

  // Notes on the sheet:
  //   INPUT A (8-bit)
  //   INPUT B (8-bit)
  //   B[2:0] extractor for shift
  //   5: SHL (use B[2:0])
  //   use LT output
  //   9: EQ (A=B -> 0x01, else 0x00)
  //   use EQ output from same comparator
  //   0: ADD
  //   1: SUB
  //   2: AND
  //   3: OR
  //   4: XOR
  //   6: SHR (use B[2:0])
  //   7: MOV (just pass A through)
  //   8: LT (A<B -> 0x01, else 0x00)
  //   flag_eq (from comparator)
  //   8-BIT ALU
  //   LT MUX (sel=LT flag)
  //   0x00
  //   0x01
  //   EQ MUX (sel=EQ flag)
  //   flag_lt (from comparator)
  //   10-15: tie to 0
  //   alu_op (4-bit)
  //   RESULT MUX
  //   16-to-1, 8-bit
  //   sel = alu_op
  //   0:ADD
  //   1:SUB
  //   2:AND
  //   3:OR
  //   4:XOR
  //   5:SHL
  //   6:SHR
  //   7:MOV
  //   8:LT
  //   9:EQ
  //   OUTPUT: result (8-bit)
endmodule

// REGS
module RegisterFile (
  input  clk,
  input  rst,
  input  [1:0] sel_rs1,
  input  we,
  input  [1:0] sel_rd,
  input  [1:0] sel_rs2,
  input  [7:0] data_in,
  output [7:0] rs1_out,
  output [7:0] rs2_out,
  output [7:0] r2_out,
  output [7:0] r3_out
);

  wire demultiplexer_1_out0, demultiplexer_1_out1, demultiplexer_1_out2, demultiplexer_1_out3;
  wire [7:0] register_1_q, register_2_q;

  Demultiplexer #(.select(2)) demultiplexer_1 (
    .out0(demultiplexer_1_out0), .out1(demultiplexer_1_out1), .out2(demultiplexer_1_out2),
    .out3(demultiplexer_1_out3), .in(we), .sel(sel_rd));
  Register register_1 (.D(data_in), .en(demultiplexer_1_out0), .clk(clk), .Q(register_1_q), .clr(rst));
  Register register_2 (.D(data_in), .en(demultiplexer_1_out1), .clk(clk), .Q(register_2_q), .clr(rst));
  Register register_3 (.D(data_in), .en(demultiplexer_1_out2), .clk(clk), .Q(r2_out), .clr(rst));
  Register register_4 (.D(data_in), .en(demultiplexer_1_out3), .clk(clk), .Q(r3_out), .clr(rst));
  Multiplexer #(.select(2), .width(8)) multiplexer_1 (
    .in0(register_1_q), .in1(register_2_q), .in2(r2_out), .in3(r3_out), .out(rs1_out), .sel(sel_rs1));
  Multiplexer #(.select(2), .width(8)) multiplexer_2 (
    .in0(register_1_q), .in1(register_2_q), .in2(r2_out), .in3(r3_out), .out(rs2_out), .sel(sel_rs2));

  // Notes on the sheet:
  //   clk
  //   rst (async)
  //   we (write enable)
  //   sel_rd (2-bit)
  //   data_in (8-bit)
  //   WRITE DEMUX
  //   in=we, sel=sel_rd
  //   R0 (en from demux[0])
  //   R1 (en from demux[1])
  //   R2 (en from demux[2])
  //   R3 (en from demux[3])
  //   REGISTER FILE (4x8-bit)
  //   R0=00, R1=01, R2=10, R3=11
  //   RS1 MUX
  //   sel=sel_rs1
  //   0:R0 1:R1 2:R2 3:R3
  //   sel_rs1 (2-bit)
  //   RS2 MUX
  //   sel=sel_rs2
  //   sel_rs2 (2-bit)
  //   R2 always out (display)
  //   R3 always out (comparison dest)
endmodule

// PC
module ProgramCounter (
  input  clk,
  input  rst,
  input  [3:0] jump_addr,
  input  halt,
  input  jump,
  input  branch,
  input  branch_cond,
  input  [7:0] rcond_val,
  output [3:0] pc_out
);

  wire and_1_out, comparator_1_eq, not_1_out, or_1_out, xor_1_out;
  wire [3:0] adder_1_out, multiplexer_1_out;

  Register #(.width(4)) register_1 (.D(multiplexer_1_out), .en(not_1_out), .clk(clk), .Q(pc_out), .clr(rst));
  not not_1 (not_1_out, halt);
  Comparator comparator_1 (.a(rcond_val), .b({8{1'b0}}), .eq(comparator_1_eq));  // open: gt, lt
  Adder #(.width(4)) adder_1 (.a(pc_out), .b(4'b0001), .out(adder_1_out));  // open: cin, cout
  xor xor_1 (xor_1_out, branch_cond, comparator_1_eq);
  or or_1 (or_1_out, jump, and_1_out);
  and and_1 (and_1_out, branch, xor_1_out);
  Multiplexer #(.width(4)) multiplexer_1 (.in0(adder_1_out), .in1(jump_addr), .out(multiplexer_1_out), .sel(or_1_out));

  // Notes on the sheet:
  //   0=JZ, 1=JNZ
  //   Compare rcond_val vs 0x00
  //   NOT halt -> write enable
  //   CONTROL INPUTS:
  //   rcond_val (8-bit register value)
  //   4-BIT PC REGISTER
  //   BRANCH LOGIC
  //   JZ(cond=0): taken when zero=1 → XOR=1
  //   JNZ(cond=1): taken when zero=0 → XOR=1
  //   branch_taken = branch_cond XOR rcond_is_zero
  //   PROGRAM COUNTER (v4.0 — 4-bit, Rcond branch)
  //   PC + 1
  //   jump_addr[3:0] from decoder
  //   take_jump = jump OR cond_jump
  //   cond_jump = branch AND branch_taken
  //   NEXT PC MUX (4-bit)
  //   0=PC+1, 1=jump_addr[3:0]
  //   OUTPUT: pc_out[3:0]
  //   LOGIC:
  //   rcond_is_zero = (rcond_val == 0x00)       [comparator]
  //   branch_taken  = branch_cond XOR rcond_is_zero
  //   cond_jump     = branch AND branch_taken
  //   take_jump     = jump OR cond_jump
  //   next_pc       = take_jump ? jump_addr : pc + 1  [MUX]
  //   pc_reg.we     = NOT(halt)
  //   pc_out        = pc_reg.Q
endmodule

module ROM (
  input  [3:0] addr,
  input  in_2,
  output [15:0] data
);

  wire [15:0] rom_1_data, rom_2_data;

  ROM_part #(.addrWidth(4), .dataWidth(16)) rom_1 (.data(rom_1_data));  // open: addr
  ROM_part #(.addrWidth(4), .dataWidth(16)) rom_2 (.addr(addr), .data(rom_2_data));
  Multiplexer #(.width(16)) multiplexer_1 (.in0(rom_2_data), .in1(rom_2_data), .out(data), .sel(in_2));

  // Notes on the sheet:
  //   addr (4-bit) from PC
  //   contents of rom_1 (hex, n*v repeats v):
  //   a005 a401 a800 8800 cc02 680 b003
  //   contents of rom_2 (hex, n*v repeats v):
  //   a005 a802 7a00 7340 ac01 2740 c403 a401 1100 d003 a401 4980 29c0 a003 dc02 a005
  //   PROGRAM ROM (16 x 16-bit, 4-bit addr)
  //   Count to 5
  //   Batch Diverter: A=5, B=3 alternating (Option B I/O)
  //   data (16-bit instruction)
endmodule

// IO_DEC
module IODecoder (
  input  mov_group,
  input  [1:0] rs2,
  input  [3:0] opcode,
  output is_mov,
  output is_in,
  output is_out,
  output sys_err
);

  wire and_1_out, and_2_out, and_3_out, and_4_out, and_8_out, comparator_1_eq, not_1_out, not_2_out;

  not not_1 (not_1_out, rs2[0]);
  not not_2 (not_2_out, rs2[1]);
  and and_1 (and_1_out, not_1_out, not_2_out);
  and and_2 (and_2_out, rs2[0], rs2[1]);
  and and_3 (and_3_out, rs2[1], not_1_out);
  and and_4 (and_4_out, not_2_out, rs2[0]);
  Comparator #(.width(4)) comparator_1 (.a(opcode), .b(4'b1110), .eq(comparator_1_eq));  // open: gt, lt
  and and_5 (is_mov, mov_group, and_1_out);
  and and_6 (is_in, mov_group, and_2_out);
  and and_7 (is_out, mov_group, and_3_out);
  and and_8 (and_8_out, mov_group, and_4_out);
  or or_1 (sys_err, and_8_out, comparator_1_eq);

  // Notes on the sheet:
  //   INPUTS:
  //   NOT
  //   LOGIC:
  //   is_mov_sel = NOT(rs2[1]) AND NOT(rs2[0])   → AND mov_group → is_mov
  //   is_in_sel  = rs2[1] AND rs2[0]             → AND mov_group → is_in
  //   is_out_sel = rs2[1] AND NOT(rs2[0])        → AND mov_group → is_out
  //   is_err_sel = NOT(rs2[1]) AND rs2[0]        → AND mov_group → io_err
  //   sys_err = io_err OR (opcode == 0xE)
  //   I/O DECODER (Option B: MOV/IN/OUT disambiguation)
  //   Opcode 0111 is overloaded: Rs2 selects MOV/IN/OUT
  //   rs2 decode
  //   qualify w/ mov_group
  //   OUTPUTS:
endmodule

// ITEM_LATCH
module ItemPulseLatch (
  input  item_pulse,
  input  read_strobe,
  input  clk,
  input  rst,
  output [7:0] input_port,
  output latch_out
);

  wire and_1_out, not_1_out;

  not not_1 (not_1_out, read_strobe);
  and and_1 (and_1_out, input_port[0], not_1_out);
  D_Flip_Flop d_ff_1 (.D(and_1_out), .clk(clk), .Q(input_port[0]), .preset(item_pulse), .reset(rst));  // open: Qn

  assign input_port[7:1] = {7{1'b0}};
  assign latch_out = input_port[0];

  // Notes on the sheet:
  //   INPUTS:
  //   LOGIC:
  //   D = Q AND NOT(read_strobe)
  //   Preset = item_pulse (async set from sensor)
  //   Clear = rst (async reset only)
  //   CLK = gated_clk (sync clear happens on clock edge)
  //   input_port[7:0] = {7'b0, Q}  (bit 0 = ITEM_PULSE)
  //   ITEM_PULSE LATCH (Section 4.2)
  //   Async set by item_pulse, sync clear on clock edge when IN executes
  //   OUTPUTS:
endmodule

// PLATFORM
module PlatformLogic (
  input  clk,
  input  stop,
  input  fault,
  input  reboot,
  input  halt_cmd,
  input  sys_err_cmd,
  input  motor_en_cpu,
  output gated_clk,
  output cpu_rst,
  output halted,
  output alarm,
  output motor_en_pin
);

  wire d_ff_1_q, d_ff_2_q, not_1_out, not_2_out, not_3_out;

  D_Flip_Flop d_ff_1 (.D(halt_cmd), .clk(clk), .Q(d_ff_1_q), .reset(reboot));  // open: Qn, preset
  D_Flip_Flop d_ff_2 (.D(sys_err_cmd), .clk(clk), .Q(d_ff_2_q), .reset(reboot));  // open: Qn, preset
  not not_1 (not_1_out, stop);
  not not_2 (not_2_out, fault);
  and and_1 (gated_clk, clk, not_1_out, not_2_out);
  or or_1 (halted, stop, fault, d_ff_1_q, d_ff_2_q);
  not not_3 (not_3_out, halted);
  and and_2 (motor_en_pin, not_3_out, motor_en_cpu);
  or or_2 (alarm, d_ff_2_q, fault);

  assign cpu_rst = reboot;

  // Notes on the sheet:
  //   INPUTS:
  //   LOGIC:
  //   cpu_halt_latch: D flip-flop, S=halt_cmd, async CLR=reboot
  //   sys_err_latch:  D flip-flop, S=sys_err_cmd, async CLR=reboot
  //   gated_clk    = clk AND NOT(stop) AND NOT(fault)
  //   HALTED       = stop OR fault OR sys_err_latch OR cpu_halt_latch
  //   motor_en_pin = motor_en_cpu AND NOT(HALTED)
  //   alarm        = fault OR sys_err_latch
  //   cpu_rst      = reboot (passthrough)
  //   PLATFORM SAFETY LOGIC (external to CPU datapath)
  //   Implements Section 3 of ISA v4.0 spec
  //   OUTPUTS:
endmodule

// CPU
module EE8_CPU (
  input  clk,
  input  rst,
  input  [7:0] input_port,
  output [3:0] pc_out,
  output [7:0] output_port,
  output io_read,
  output sys_err_out,
  output [7:0] r2_debug,
  output halt_out
);

  wire and_1_out, controlunit_1_branch, controlunit_1_branch_cond, controlunit_1_jump,
       controlunit_1_mov_group, controlunit_1_reg_write, iodecoder_1_is_out, not_1_out;
  wire [1:0] controlunit_1_imm_sel, instructiondecoder_1_rd, instructiondecoder_1_rs1,
       instructiondecoder_1_rs2, multiplexer_1_out;
  wire [3:0] controlunit_1_alu_op, instructiondecoder_1_address, instructiondecoder_1_opcode;
  wire [7:0] alu_1_result, instructiondecoder_1_immediate, multiplexer_2_out, multiplexer_3_out,
       registerfile_1_rs1_out, registerfile_1_rs2_out;
  wire [15:0] rom_1_data;

  Multiplexer #(.select(2), .width(2)) multiplexer_1 (
    .in0(instructiondecoder_1_rd), .in1(instructiondecoder_1_rs1), .in2(2'b11), .out(multiplexer_1_out),
    .sel(controlunit_1_imm_sel));  // open: in3
  ProgramCounter programcounter_1 (
    .clk(clk), .rst(rst), .jump_addr(instructiondecoder_1_address), .halt(halt_out),
    .jump(controlunit_1_jump), .branch(controlunit_1_branch), .branch_cond(controlunit_1_branch_cond),
    .rcond_val(registerfile_1_rs1_out), .pc_out(pc_out));
  not not_1 (not_1_out, iodecoder_1_is_out);
  and and_1 (and_1_out, not_1_out, controlunit_1_reg_write);
  Multiplexer #(.width(8)) multiplexer_2 (.in0(alu_1_result), .in1(input_port), .out(multiplexer_2_out), .sel(io_read));
  ROM rom_1 (.addr(pc_out), .data(rom_1_data));  // open: in_2
  RegisterFile registerfile_1 (
    .clk(clk), .rst(rst), .sel_rs1(instructiondecoder_1_rs1), .we(and_1_out), .sel_rd(multiplexer_1_out),
    .sel_rs2(instructiondecoder_1_rs2), .data_in(multiplexer_2_out), .rs1_out(registerfile_1_rs1_out),
    .rs2_out(registerfile_1_rs2_out), .r2_out(r2_debug));  // open: r3_out
  InstructionDecoder instructiondecoder_1 (
    .instruction(rom_1_data), .rd(instructiondecoder_1_rd), .rs2(instructiondecoder_1_rs2),
    .rs1(instructiondecoder_1_rs1), .immediate(instructiondecoder_1_immediate),
    .opcode(instructiondecoder_1_opcode), .address(instructiondecoder_1_address));
  Multiplexer #(.width(8)) multiplexer_3 (
    .in0(registerfile_1_rs1_out), .in1(instructiondecoder_1_immediate), .out(multiplexer_3_out),
    .sel(controlunit_1_imm_sel[0]));
  IODecoder iodecoder_1 (
    .mov_group(controlunit_1_mov_group), .rs2(instructiondecoder_1_rs2),
    .opcode(instructiondecoder_1_opcode), .is_in(io_read), .is_out(iodecoder_1_is_out), .sys_err(sys_err_out));  // open: is_mov
  ALU alu_1 (
    .A(multiplexer_3_out), .B(registerfile_1_rs2_out), .alu_op(controlunit_1_alu_op), .result(alu_1_result));  // open: flag_eq, flag_lt
  ControlUnit controlunit_1 (
    .opcode(instructiondecoder_1_opcode), .mov_group(controlunit_1_mov_group),
    .flag_write(controlunit_1_imm_sel[1]), .halt(halt_out), .branch_cond(controlunit_1_branch_cond),
    .branch(controlunit_1_branch), .jump(controlunit_1_jump), .imm_sel(controlunit_1_imm_sel[0]),
    .reg_write(controlunit_1_reg_write), .alu_op(controlunit_1_alu_op));
  Register register_1 (.D(registerfile_1_rs1_out), .en(iodecoder_1_is_out), .Q(output_port));  // open: clk, clr

  // Notes on the sheet:
  //   EXTERNAL INPUTS:
  //   PC
  //   RD_SEL MUX (2-bit sel)
  //   sel[0]=imm_sel, sel[1]=flag_write
  //   00=rd, 01=rs1(LDI dest), 10=R3(11), 11=unused
  //   EE8 CPU v4.0 — TOP LEVEL INTEGRATION
  //   Single-cycle RISC datapath. I/O Option B (IN/OUT instructions).
  //   WRITEBACK MUX (sel=is_in)
  //   0=ALU result, 1=input_port
  //   ROM
  //   REGISTERS
  //   DECODE
  //   ALU_A MUX (sel=imm_sel)
  //   0=rs1_out, 1=immediate
  //   ALU
  //   CONTROL
  //   IO DECODER
  //   OUTPUT PORT REG (8-bit)
  //   write_en = is_out, data = rs1_out
  //   EXTERNAL OUTPUTS:
  //   === DATAPATH (v4.0) ===
  //   Single-cycle: FETCH -> DECODE -> EXECUTE -> WRITEBACK (one clock)
  //   EXECUTE LOGIC:
  //   ALU_A       = imm_sel ? immediate[7:0] : rs1_out[7:0]
  //   ALU_B       = rs2_out[7:0]
  //   alu_result  = ALU(ALU_A, ALU_B, alu_op)
  //   WRITEBACK LOGIC:
  //   data_in     = is_in ? input_port : alu_result
  //   rd_sel      = {flag_write, imm_sel}: 00=rd[7:6], 01=rs1[11:10](LDI), 10=R3(LT/EQ)
  //   reg_we      = reg_write AND NOT(is_out)
  //   I/O (Option B — opcode 0111 overloaded):
  //   IO_DEC decodes rs2: 00=MOV, 10=OUT, 11=IN, 01=SYS_ERR
  //   OUT: output_port_reg latches rs1_out on is_out
  //   IN:  input_port routed to reg file via writeback MUX on is_in
  //   sys_err = io_err OR (opcode == 0xE)
  //   DEBUG PINS:
  //   pc_out, r2_debug, io_read, halt_out, sys_err_out — exposed for test bench
  //     01 (LDI):    DECODE.rs1[1:0] -> REGS.sel_rd (I-type Rd is at rs1 position [11:10])
  //   REGS.rs1_out[7:0] -> PC.rcond_val[7:0]  (Rcond = rs1 field = any register)
  //   CTRL.halt -> PC.halt AND halt_out pin
  //   DECODE.opcode[3:0] -> IO_DEC.opcode (for reserved opcode 1110 detect)
  //   IO_DEC.is_in -> io_read pin (for external ITEM_PULSE latch clear)
endmodule

module main (
  input  STOP,
  input  FAULT,
  input  RESET
);

  wire and_1_out, CLK_out, ee8_cpu_1_halt_out, ee8_cpu_1_io_read, ee8_cpu_1_sys_err_out, INPUT_PULSE_out,
       itempulselatch_1_latch_out, not_1_out, platformlogic_1_alarm, platformlogic_1_cpu_rst,
       platformlogic_1_gated_clk, platformlogic_1_halted, platformlogic_1_motor_en_pin;
  wire [3:0] ee8_cpu_1_pc_out;
  wire [7:0] ee8_cpu_1_output_port, ee8_cpu_1_r2_debug, itempulselatch_1_input_port;

  Clock CLK (.out(CLK_out));
  and and_1 (and_1_out, ee8_cpu_1_r2_debug[1], not_1_out);
  not not_1 (not_1_out, ee8_cpu_1_halt_out);
  Button INPUT_PULSE (.out(INPUT_PULSE_out));
  PlatformLogic platformlogic_1 (
    .clk(CLK_out), .stop(STOP), .fault(FAULT), .reboot(RESET), .halt_cmd(ee8_cpu_1_halt_out),
    .sys_err_cmd(ee8_cpu_1_sys_err_out), .motor_en_cpu(and_1_out), .gated_clk(platformlogic_1_gated_clk),
    .cpu_rst(platformlogic_1_cpu_rst), .halted(platformlogic_1_halted), .alarm(platformlogic_1_alarm),
    .motor_en_pin(platformlogic_1_motor_en_pin));
  ItemPulseLatch itempulselatch_1 (
    .item_pulse(INPUT_PULSE_out), .read_strobe(ee8_cpu_1_io_read), .clk(platformlogic_1_gated_clk),
    .rst(platformlogic_1_cpu_rst), .input_port(itempulselatch_1_input_port),
    .latch_out(itempulselatch_1_latch_out));
  LED ITEM_LATCH (.in(itempulselatch_1_latch_out));
  LED HALTED (.in(platformlogic_1_halted));
  LED ALARM (.in(platformlogic_1_alarm));
  LED MOTOR_PIN (.in(platformlogic_1_motor_en_pin));
  EE8_CPU ee8_cpu_1 (
    .clk(platformlogic_1_gated_clk), .rst(platformlogic_1_cpu_rst), .input_port(itempulselatch_1_input_port),
    .pc_out(ee8_cpu_1_pc_out), .output_port(ee8_cpu_1_output_port), .io_read(ee8_cpu_1_io_read),
    .sys_err_out(ee8_cpu_1_sys_err_out), .r2_debug(ee8_cpu_1_r2_debug), .halt_out(ee8_cpu_1_halt_out));
  LED GATE_SEL (.in(ee8_cpu_1_r2_debug[0]));
  LED MOTOR_EN (.in(ee8_cpu_1_r2_debug[1]));
  Hex_Digit_Display hex_digit_display_1 (.value(ee8_cpu_1_pc_out));  // open: dp
  Hex_Digit_Display hex_digit_display_2 (.value(ee8_cpu_1_output_port[7:4]));  // open: dp
  Hex_Digit_Display hex_digit_display_3 (.value(ee8_cpu_1_output_port[3:0]));  // open: dp
  Hex_Digit_Display hex_digit_display_4 (.value(ee8_cpu_1_r2_debug[7:4]));  // open: dp
  Hex_Digit_Display hex_digit_display_5 (.value(ee8_cpu_1_r2_debug[3:0]));  // open: dp

  // Notes on the sheet:
  //   Platform signals
  //   EE8 CPU
  //   splitter [7:4][3:0] for hex; tap bit0=GATE_SEL, bit1=MOTOR_EN
  //   EE8 CPU v4.0
  //   PC 
  //   Output Port
  //   R2 splitter [7:4][3:0]
  //   Out High
  //   Out Low
  //   R2 High
  //   R2 Low
  //   TEST BENCH GUIDE:
  //   1. Toggle RESET to initialise, 2. Ctrl+K to tick clock
  //   3. Toggle INPUT_PULSE to simulate item sensor
  //   INPUT PINS:
  //   CLK          System clock
  //   RESET        Async reset (clears all state, PC=0)
  //   STOP         Operator pause (clock gated, state preserved)
  //   FAULT        Hardware fault (clock gated + ALARM)
  //   INPUT_PULSE  Item sensor (sets ITEM_PULSE latch)
  //   DISPLAYS:
  //   PC hex         Current program counter value
  //   R2 High/Low    Register R2 value (debug)
  //   Out High/Low   Output port value [7:0]
  //   LEDs:
  //   GATE_SEL     Output port bit 0 (0=Gate A, 1=Gate B)
  //   MOTOR_EN     Output port bit 1 (motor enable request)
  //   HALTED       Any halt source active (STOP|FAULT|SYS_ERR|CPU_HALT)
  //   ALARM        Fault condition (FAULT|SYS_ERR, not STOP/HALT)
  //   MOTOR_PIN    Actual motor output after safety interlock
  //   ITEM_LATCH   ITEM_PULSE latch state (debug)
endmodule
