// Logisim project pc_tflipflop.circ as structural Verilog: 1 circuit, main circuit ProgramCounter_TFF
// PC
module ProgramCounter_TFF (
  input  RST,
  input  JMP_EN,
  input  CLK,
  input  [3:0] ADDR,
  output [3:0] PC_OUT
);

  wire and_1_out, and_2_out, and_3_out, and_4_out, and_5_out, and_6_out, and_7_out, and_8_out, and_9_out,
       and_10_out, and_11_out, not_1_out, not_2_out, not_3_out, not_4_out, not_5_out, not_6_out, or_1_out,
       or_2_out, or_3_out, or_4_out;

  not not_1 (not_1_out, JMP_EN);
  not not_2 (not_2_out, RST);
  not not_3 (not_3_out, ADDR[0]);
  and and_1 (and_1_out, not_3_out, JMP_EN);
  and and_2 (and_2_out, not_2_out, JMP_EN, ADDR[0]);
  T_Flip_Flop t_ff_1 (.clk(CLK), .T(not_1_out), .Q(PC_OUT[0]), .preset(and_2_out), .reset(or_1_out));  // open: Qn, en
  or or_1 (or_1_out, and_1_out, RST);
  not not_4 (not_4_out, ADDR[1]);
  and and_3 (and_3_out, not_4_out, JMP_EN);
  or or_2 (or_2_out, and_3_out, RST);
  and and_4 (and_4_out, not_2_out, JMP_EN, ADDR[1]);
  and and_5 (and_5_out, PC_OUT[0], not_1_out);
  T_Flip_Flop t_ff_2 (.clk(CLK), .T(and_5_out), .Q(PC_OUT[1]), .preset(and_4_out), .reset(or_2_out));  // open: Qn, en
  not not_5 (not_5_out, ADDR[2]);
  T_Flip_Flop t_ff_3 (.clk(CLK), .T(and_8_out), .Q(PC_OUT[2]), .preset(and_7_out), .reset(or_3_out));  // open: Qn, en
  or or_3 (or_3_out, and_6_out, RST);
  and and_6 (and_6_out, not_5_out, JMP_EN);
  and and_7 (and_7_out, not_2_out, JMP_EN, ADDR[2]);
  and and_8 (and_8_out, PC_OUT[1], and_5_out);
  not not_6 (not_6_out, ADDR[3]);
  and and_9 (and_9_out, not_6_out, JMP_EN);
  and and_10 (and_10_out, PC_OUT[2], and_8_out);
  T_Flip_Flop t_ff_4 (.clk(CLK), .T(and_10_out), .Q(PC_OUT[3]), .preset(and_11_out), .reset(or_4_out));  // open: Qn, en
  or or_4 (or_4_out, and_9_out, RST);
  and and_11 (and_11_out, not_2_out, JMP_EN, ADDR[3]);

  // Notes on the sheet:
  //   bit0 (LSB) top
  //   bit3 (MSB) bottom
  //   NOT_JMP_EN
  //   NOT_RST
  //   NOT_A0
  //   JMP&!A0
  //   BIT 0 (LSB)
  //   T0 = NOT_JMP_EN
  //   SET0 -> pin '1'
  //   Q0
  //   CLR0 -> pin '0'
  //   4-BIT PROGRAM COUNTER (T Flip-Flops)
  //   Priority: RST (all zero) > JMP (load addr) > Count (increment)
  //   NOT_A1
  //   JMP&!A1
  //   T1 = NOT_JMP & Q0
  //   BIT 1
  //   SET1 -> pin '1'
  //   Q1
  //   CLR1 -> pin '0'
  //   JMP&!A2
  //   NOT_A2
  //   BIT 2
  //   SET2 -> pin '1'
  //   T2 = T1 & Q1
  //   Q2
  //   CLR2 -> pin '0'
  //   JMP&!A3
  //   NOT_A3
  //   BIT 3 (MSB)
  //   SET3 -> pin '1'
  //   T3 = T2 & Q2
  //   Q3
  //   CLR3 -> pin '0'
  //   !RST
  //   RST
  //   CLK
  //   JMP_EN
endmodule
