// Logisim project program_counter.circ as structural Verilog: 1 circuit, main circuit ProgramCounter
module ProgramCounter (
  input  JMP,
  input  ADDR0,
  input  ADDR1,
  input  ADDR2,
  input  ADDR3,
  input  CLK,
  input  RST,
  output PC0,
  output PC1,
  output PC2,
  output PC3
);

  wire xor_3_out, xor_4_out;

  // XOR_Gate xor_1 is placed but not wired
  // XOR_Gate xor_2 is placed but not wired
  // AND_Gate and_1 has open pins: in1=xor_3_out, out=open
  // XOR_Gate xor_3 has open pins: out=xor_3_out
  // AND_Gate and_2 has open pins: in2=xor_4_out, out=open
  // XOR_Gate xor_4 has open pins: out=xor_4_out
  Multiplexer multiplexer_1 ();  // open: in0, in1, out, sel, en
  Multiplexer multiplexer_2 ();  // open: in0, in1, out, sel, en
  Multiplexer multiplexer_3 ();  // open: in0, in1, out, sel, en
  Multiplexer multiplexer_4 ();  // open: in0, in1, out, sel, en
  T_Flip_Flop t_ff_1 ();  // open: clk, T, Q, Qn, preset, reset, en
  T_Flip_Flop t_ff_2 ();  // open: clk, T, Q, Qn, preset, reset, en
  T_Flip_Flop t_ff_3 ();  // open: clk, T, Q, Qn, preset, reset, en
  T_Flip_Flop t_ff_4 ();  // open: clk, T, Q, Qn, preset, reset, en

  // Notes on the sheet:
  //   EE8 PROGRAM COUNTER
  //   4-bit counter with JMP and RST
endmodule
